// Logisim project Guia_0701.circ as structural Verilog: 1 circuit, main circuit main
module main (
  input  x,
  input  y,
  input  s,
  output z
);

  wire AND_out, NAND_out;

  and AND (AND_out, x, y);
  nand NAND (NAND_out, x, y);
  Multiplexer #(.enable("false")) multiplexer_1 (.in0(AND_out), .in1(NAND_out), .out(z), .sel(s));

  // Notes on the sheet:
  //   Guia_0701
  //   Vinícius Miranda de Araújo - 812839
endmodule
