// Logisim project Guia_0702.circ as structural Verilog: 1 circuit, main circuit main
module main (
  input  x,
  input  y,
  input  s,
  output z
);

  wire NOR_out, OR_out;

  or OR (OR_out, x, y);
  nor NOR (NOR_out, x, y);
  Multiplexer #(.enable("false")) multiplexer_1 (.in0(OR_out), .in1(NOR_out), .out(z), .sel(s));

  // Notes on the sheet:
  //   Guia_0702
  //   Vinícius Miranda de Araújo - 812839
endmodule
