// Logisim project Guia_0703.circ as structural Verilog: 1 circuit, main circuit main
module main (
  input  x,
  input  y,
  input  s1,
  input  S3,
  input  s2,
  output z
);

  wire AND_out, multiplexer_1_out, multiplexer_2_out, NAND_out, NOR_out, OR_out;

  and AND (AND_out, x, y);
  nand NAND (NAND_out, x, y);
  or OR (OR_out, x, y);
  nor NOR (NOR_out, x, y);
  Multiplexer #(.enable("false")) multiplexer_1 (.in0(AND_out), .in1(NAND_out), .out(multiplexer_1_out), .sel(s1));
  Multiplexer #(.enable("false")) multiplexer_2 (.in0(OR_out), .in1(NOR_out), .out(multiplexer_2_out), .sel(s2));
  Multiplexer #(.enable("false")) multiplexer_3 (.in0(multiplexer_1_out), .in1(multiplexer_2_out), .out(z), .sel(S3));

  // Notes on the sheet:
  //   Guia_0703
  //   Vinícius Miranda de Araújo - 812839
endmodule
