// Logisim project Guia_0704.circ as structural Verilog: 1 circuit, main circuit main
module main (
  input  x,
  input  y,
  input  [1:0] s1_s2,
  output z
);

  wire NOR_out, OR_out, XNOR_out, XOR_out;

  or OR (OR_out, x, y);
  nor NOR (NOR_out, x, y);
  xor XOR (XOR_out, x, y);
  xnor XNOR (XNOR_out, x, y);
  Multiplexer #(.select(2), .enable("false")) multiplexer_1 (
    .in0(OR_out), .in1(NOR_out), .in2(XOR_out), .in3(XNOR_out), .out(z), .sel(s1_s2));

  // Notes on the sheet:
  //   Guia_0704
  //   Vinícius Miranda de Araújo - 812839
endmodule
