// Logisim project Guia_0705.circ as structural Verilog: 1 circuit, main circuit main
module main (
  input  x,
  input  y,
  input  [2:0] select,
  output z
);

  wire AND_out, NAND_out, NOR_out, NOT_X_out, NOT_Y_out, OR_out, XNOR_out, XOR_out;

  not NOT_X (NOT_X_out, x);
  not NOT_Y (NOT_Y_out, y);
  and AND (AND_out, x, y);
  nand NAND (NAND_out, x, y);
  or OR (OR_out, x, y);
  nor NOR (NOR_out, x, y);
  xor XOR (XOR_out, x, y);
  xnor XNOR (XNOR_out, x, y);
  Multiplexer #(.select(3), .enable("false")) multiplexer_1 (
    .in0(NOT_X_out), .in1(NOT_Y_out), .in2(AND_out), .in3(NAND_out), .in4(OR_out), .in5(NOR_out),
    .in6(XOR_out), .in7(XNOR_out), .out(z), .sel(select));

  // Notes on the sheet:
  //   Guia_0705
  //   Vinícius Miranda de Araújo - 812839
endmodule
